// Logisim project cpu.circ as structural Verilog: 7 circuits, main circuit main
module OPDEC (
  input  op0,
  input  op1,
  input  op2,
  input  op3,
  input  op4,
  output alu0,
  output alu1,
  output mem0,
  output mem1,
  output br0,
  output br1,
  output br2
);

  wire and_1_out, and_2_out, and_3_out, and_4_out, and_5_out, and_6_out, and_7_out, and_8_out, and_9_out,
       and_10_out, and_11_out, and_12_out, and_13_out, and_14_out, and_15_out, and_16_out, and_17_out,
       and_18_out, and_19_out, and_20_out, and_21_out, and_22_out, and_23_out, and_24_out, not_1_out,
       not_2_out, not_3_out, not_4_out, not_5_out, not_6_out, not_7_out, not_8_out, not_9_out, not_10_out,
       not_11_out, not_12_out, not_13_out, not_14_out, not_15_out, not_16_out, not_17_out, not_18_out,
       not_19_out, not_20_out, not_21_out, not_22_out, not_23_out, not_24_out, not_25_out, not_26_out,
       not_27_out, not_28_out, not_29_out, not_30_out, not_31_out, not_32_out, not_33_out, not_34_out,
       not_35_out, not_36_out, not_37_out, not_38_out, not_39_out;

  not not_1 (not_1_out, op0);
  not not_2 (not_2_out, op3);
  not not_3 (not_3_out, op4);
  not not_4 (not_4_out, op0);
  not not_5 (not_5_out, op2);
  not not_6 (not_6_out, op2);
  not not_7 (not_7_out, op3);
  not not_8 (not_8_out, op4);
  not not_9 (not_9_out, op1);
  not not_10 (not_10_out, op1);
  not not_11 (not_11_out, op4);
  not not_12 (not_12_out, op1);
  not not_13 (not_13_out, op0);
  not not_14 (not_14_out, op3);
  not not_15 (not_15_out, op4);
  not not_16 (not_16_out, op0);
  not not_17 (not_17_out, op2);
  not not_18 (not_18_out, op1);
  not not_19 (not_19_out, op0);
  not not_20 (not_20_out, op1);
  not not_21 (not_21_out, op1);
  not not_22 (not_22_out, op2);
  not not_23 (not_23_out, op2);
  not not_24 (not_24_out, op1);
  not not_25 (not_25_out, op3);
  not not_26 (not_26_out, op1);
  not not_27 (not_27_out, op4);
  not not_28 (not_28_out, op2);
  not not_29 (not_29_out, op3);
  not not_30 (not_30_out, op4);
  not not_31 (not_31_out, op1);
  not not_32 (not_32_out, op2);
  not not_33 (not_33_out, op3);
  not not_34 (not_34_out, op4);
  not not_35 (not_35_out, op4);
  and and_1 (and_1_out, not_1_out, op2, not_2_out, not_3_out);
  and and_2 (and_2_out, not_4_out, op1, not_5_out, op3);
  and and_3 (and_3_out, op0, not_6_out, not_7_out, not_8_out);
  and and_4 (and_4_out, op0, not_9_out, op3, op4);
  and and_5 (and_5_out, op0, not_10_out, op2);
  and and_6 (and_6_out, op0, op2, op3, not_11_out);
  and and_7 (and_7_out, not_12_out, op3, op4);
  and and_8 (and_8_out, not_13_out, op2, not_14_out, not_15_out);
  and and_9 (and_9_out, not_16_out, op1, not_17_out, op3);
  and and_10 (and_10_out, op0, not_18_out);
  and and_11 (and_11_out, not_19_out, not_20_out);
  and and_12 (and_12_out, not_21_out, not_22_out);
  not not_36 (not_36_out, op3);
  and and_13 (and_13_out, op1, op2);
  and and_14 (and_14_out, op0, not_23_out);
  or or_1 (mem1, not_24_out, not_25_out, op4, op2, op0);
  not not_37 (not_37_out, op0);
  and and_15 (and_15_out, not_26_out, op2, op3, not_27_out);
  and and_16 (and_16_out, op1, op4);
  and and_17 (and_17_out, op1, not_28_out, op3);
  and and_18 (and_18_out, op1, op2, not_29_out);
  not not_38 (not_38_out, op0);
  and and_19 (and_19_out, op2, op3, not_30_out);
  not not_39 (not_39_out, op0);
  and and_20 (and_20_out, not_31_out, not_32_out, not_33_out, not_34_out);
  and and_21 (and_21_out, op2, op3, not_35_out);
  and and_22 (and_22_out, op1, op4);
  and and_23 (and_23_out, op1, op3);
  and and_24 (and_24_out, op1, op2);
  or or_2 (alu0, and_1_out, and_2_out, and_3_out, and_4_out, and_5_out, and_6_out);
  or or_3 (alu1, and_7_out, and_8_out, and_9_out, and_10_out);
  or or_4 (mem0, and_11_out, and_12_out, not_36_out, op4, and_13_out, and_14_out);
  or or_5 (br0, not_37_out, and_15_out, and_16_out, and_17_out, and_18_out);
  or or_6 (br1, not_38_out, and_19_out, op1);
  or or_7 (br2, not_39_out, and_20_out, and_21_out, and_22_out, and_23_out, and_24_out);
endmodule

module FSM (
  input  [15:0] IN,
  input  CLK,
  input  RST,
  output [31:0] OUT
);

  wire pull_resistor_1_node, pull_resistor_3_node;
  wire [1:0] nand_1_out, opdec_1_alu0, opdec_1_mem1;
  wire [2:0] multiplexer_1_out, State_q;
  wire [4:4] or_1_out;
  wire [6:0] multiplexer_2_out;
  wire [6:3] State_q_2;

  OPDEC opdec_1 (
    .op0(IN[14]), .op1(IN[13]), .op2(IN[12]), .op3(IN[11]), .op4(IN[10]), .alu0(opdec_1_alu0[0]),
    .alu1(opdec_1_alu0[1]), .mem0(opdec_1_mem1[1]), .mem1(opdec_1_mem1[0]));  // open: br0, br1, br2
  nand nand_1 (nand_1_out[0], opdec_1_alu0[0], opdec_1_alu0[1]);
  nand nand_2 (nand_1_out[1], opdec_1_mem1[1], opdec_1_mem1[0]);
  Multiplexer #(.select(2), .width(3), .enable("false")) multiplexer_1 (
    .in1({IN[15], opdec_1_alu0}), .in2({1'b0, opdec_1_mem1}), .out(multiplexer_1_out), .sel(nand_1_out));  // open: in0, in3
  or or_1 (or_1_out[4], nand_1_out[0], nand_1_out[1]);
  Pull_Resistor #(.pull(1)) pull_resistor_1 (.node(pull_resistor_1_node));
  Register #(.width(7)) State (
    .D(multiplexer_2_out), .en(pull_resistor_1_node), .Q({State_q_2, State_q}), .clk(CLK), .clr(RST));
  Pull_Resistor pull_resistor_2 (.node(RST));
  Multiplexer #(.select(3), .width(7), .enable("false")) multiplexer_2 (
    .in0(7'b0001000), .in1({2'b00, or_1_out[4], nand_1_out[1], multiplexer_1_out}), .in2({7{1'b0}}),
    .in3({4'b0100, State_q}), .in4({7{1'b0}}), .out(multiplexer_2_out), .sel(State_q_2[5:3]));  // open: in5, in6, in7
  ROM #(.addrWidth(7), .dataWidth(32)) rom_1 (.addr({State_q_2, State_q}), .data(OUT), .sel(pull_resistor_3_node));
  Pull_Resistor #(.pull(1)) pull_resistor_3 (.node(pull_resistor_3_node));

  // Notes on the sheet:
  //   IMM
  //   OP0 is MSB
  //   IS_ALU
  //   IS_MEM
  //   contents of rom_1 (hex, n*v repeats v):
  //   48000000 7*0 80000000 7*0 6000015 6000016 0 0 6000010 6000010 0 0 e000105 32000101
endmodule

module REG4 (
  input  [1:0] RSEL2,
  input  WE,
  input  [1:0] RSEL1,
  input  [1:0] WSEL,
  input  [31:0] DATAIN,
  input  CLK,
  input  RST,
  output [31:0] DATAOUT1,
  output [31:0] DATAOUT2
);

  wire decoder_1_out0, decoder_1_out1, decoder_1_out2, decoder_1_out3;
  wire [31:0] multiplexer_1_out, multiplexer_2_out, multiplexer_4_out, multiplexer_5_out, register_1_q,
       register_2_q, register_3_q, register_4_q;

  Decoder #(.select(2), .disabled(0)) decoder_1 (
    .out0(decoder_1_out0), .out1(decoder_1_out1), .out2(decoder_1_out2), .out3(decoder_1_out3), .sel(WSEL),
    .en(WE));
  Register #(.width(32)) register_1 (.D(DATAIN), .en(decoder_1_out0), .Q(register_1_q), .clk(CLK), .clr(RST));
  Register #(.width(32)) register_2 (.D(DATAIN), .en(decoder_1_out1), .Q(register_2_q), .clk(CLK), .clr(RST));
  Register #(.width(32)) register_3 (.D(DATAIN), .en(decoder_1_out2), .Q(register_3_q), .clk(CLK), .clr(RST));
  Register #(.width(32)) register_4 (.D(DATAIN), .en(decoder_1_out3), .Q(register_4_q), .clk(CLK), .clr(RST));
  Multiplexer #(.width(32), .enable("false")) multiplexer_1 (
    .in0(register_1_q), .in1(register_2_q), .out(multiplexer_1_out), .sel(RSEL1[0]));
  Multiplexer #(.width(32), .enable("false")) multiplexer_2 (
    .in0(register_3_q), .in1(register_4_q), .out(multiplexer_2_out), .sel(RSEL1[0]));
  Multiplexer #(.width(32), .enable("false")) multiplexer_3 (
    .in0(multiplexer_1_out), .in1(multiplexer_2_out), .out(DATAOUT1), .sel(RSEL1[1]));
  Multiplexer #(.width(32), .enable("false")) multiplexer_4 (
    .in0(register_1_q), .in1(register_2_q), .out(multiplexer_4_out), .sel(RSEL2[0]));
  Multiplexer #(.width(32), .enable("false")) multiplexer_5 (
    .in0(register_3_q), .in1(register_4_q), .out(multiplexer_5_out), .sel(RSEL2[0]));
  Multiplexer #(.width(32), .enable("false")) multiplexer_6 (
    .in0(multiplexer_4_out), .in1(multiplexer_5_out), .out(DATAOUT2), .sel(RSEL2[1]));
endmodule

module REG16 (
  input  [3:0] in_1,
  input  [3:0] in_2,
  input  [3:0] in_3,
  input  in_4,
  input  [31:0] DATAIN,
  input  in_6,
  input  in_7,
  output [31:0] out_8,
  output [31:0] out_9
);

  wire decoder_1_out0, decoder_1_out1, decoder_1_out2, decoder_1_out3;
  wire [31:0] multiplexer_1_out, multiplexer_2_out, multiplexer_4_out, multiplexer_5_out, reg4_1_dataout1,
       reg4_1_dataout2, reg4_2_dataout1, reg4_2_dataout2, reg4_3_dataout1, reg4_3_dataout2, reg4_4_dataout1,
       reg4_4_dataout2;

  Decoder #(.select(2), .disabled(0)) decoder_1 (
    .out0(decoder_1_out0), .out1(decoder_1_out1), .out2(decoder_1_out2), .out3(decoder_1_out3),
    .sel(in_1[3:2]), .en(in_4));
  REG4 reg4_1 (
    .RSEL2(in_3[1:0]), .WE(decoder_1_out0), .RSEL1(in_2[1:0]), .WSEL(in_1[1:0]), .DATAIN(DATAIN),
    .DATAOUT1(reg4_1_dataout1), .DATAOUT2(reg4_1_dataout2), .CLK(in_6), .RST(in_7));
  REG4 reg4_2 (
    .RSEL2(in_3[1:0]), .WE(decoder_1_out1), .RSEL1(in_2[1:0]), .WSEL(in_1[1:0]), .DATAIN(DATAIN),
    .DATAOUT1(reg4_2_dataout1), .DATAOUT2(reg4_2_dataout2), .CLK(in_6), .RST(in_7));
  REG4 reg4_3 (
    .RSEL2(in_3[1:0]), .WE(decoder_1_out2), .RSEL1(in_2[1:0]), .WSEL(in_1[1:0]), .DATAIN(DATAIN),
    .DATAOUT1(reg4_3_dataout1), .DATAOUT2(reg4_3_dataout2), .CLK(in_6), .RST(in_7));
  REG4 reg4_4 (
    .RSEL2(in_3[1:0]), .WE(decoder_1_out3), .RSEL1(in_2[1:0]), .WSEL(in_1[1:0]), .DATAIN(DATAIN),
    .DATAOUT1(reg4_4_dataout1), .DATAOUT2(reg4_4_dataout2), .CLK(in_6), .RST(in_7));
  Multiplexer #(.width(32), .enable("false")) multiplexer_1 (
    .in0(reg4_1_dataout1), .in1(reg4_2_dataout1), .out(multiplexer_1_out), .sel(in_2[2]));
  Multiplexer #(.width(32), .enable("false")) multiplexer_2 (
    .in0(reg4_3_dataout1), .in1(reg4_4_dataout1), .out(multiplexer_2_out), .sel(in_2[2]));
  Multiplexer #(.width(32), .enable("false")) multiplexer_3 (
    .in0(multiplexer_1_out), .in1(multiplexer_2_out), .out(out_8), .sel(in_2[3]));
  Multiplexer #(.width(32), .enable("false")) multiplexer_4 (
    .in0(reg4_1_dataout2), .in1(reg4_2_dataout2), .out(multiplexer_4_out), .sel(in_3[2]));
  Multiplexer #(.width(32), .enable("false")) multiplexer_5 (
    .in0(reg4_3_dataout2), .in1(reg4_4_dataout2), .out(multiplexer_5_out), .sel(in_3[2]));
  Multiplexer #(.width(32), .enable("false")) multiplexer_6 (
    .in0(multiplexer_4_out), .in1(multiplexer_5_out), .out(out_9), .sel(in_3[3]));
endmodule

// REGS
module REG32 (
  input  [4:0] in_1,
  input  [4:0] in_2,
  input  [4:0] in_3,
  input  in_4,
  input  [31:0] in_5,
  input  in_6,
  input  in_7,
  output [31:0] out_8,
  output [31:0] out_9
);

  wire decoder_1_out0, decoder_1_out1;
  wire [31:0] reg16_1_out_8, reg16_1_out_9, reg16_2_out_8, reg16_2_out_9;

  Decoder #(.disabled(0)) decoder_1 (.out0(decoder_1_out0), .out1(decoder_1_out1), .sel(in_1[4]), .en(in_4));
  REG16 reg16_1 (
    .in_1(in_1[3:0]), .in_2(in_2[3:0]), .in_3(in_3[3:0]), .in_4(decoder_1_out0), .DATAIN(in_5),
    .out_8(reg16_1_out_8), .out_9(reg16_1_out_9), .in_6(in_6), .in_7(in_7));
  REG16 reg16_2 (
    .in_1(in_1[3:0]), .in_2(in_2[3:0]), .in_3(in_3[3:0]), .in_4(decoder_1_out1), .DATAIN(in_5),
    .out_8(reg16_2_out_8), .out_9(reg16_2_out_9), .in_6(in_6), .in_7(in_7));
  Multiplexer #(.width(32), .enable("false")) multiplexer_1 (
    .in0(reg16_1_out_8), .in1(reg16_2_out_8), .out(out_8), .sel(in_2[4]));
  Multiplexer #(.width(32), .enable("false")) multiplexer_2 (
    .in0(reg16_1_out_9), .in1(reg16_2_out_9), .out(out_9), .sel(in_3[4]));
endmodule

module ALU (
  input  [4:0] Sel,
  input  [31:0] A,
  input  [31:0] B,
  output [31:0] Result,
  output [2:0] Status
);

  wire comparator_2_eq;
  wire [0:0] and_2_out, and_3_out, comparator_2_gt, not_1_out;
  wire [31:0] adder_1_out, and_1_out, divider_1_out, divider_1_rem, multiplexer_1_out, multiplexer_2_out,
       multiplexer_3_out, multiplexer_4_out, multiplexer_5_out, multiplexer_6_out, multiplexer_7_out,
       multiplexer_8_out, multiplexer_9_out, multiplexer_10_out, multiplexer_11_out, multiplexer_12_out,
       multiplexer_13_out, multiplexer_14_out, multiplexer_15_out, multiplexer_16_out, multiplexer_17_out,
       multiplexer_18_out, multiplexer_19_out, multiplexer_20_out, multiplexer_21_out, multiplexer_22_out,
       multiplexer_23_out, multiplier_1_out, nor_1_out, or_1_out, shifter_1_out, shifter_2_out,
       shifter_3_out, subtractor_1_out, xnor_1_out, xor_1_out;

  Comparator #(.width(32)) comparator_1 (.a(A), .b(B), .gt(Status[0]), .eq(Status[1]));  // open: lt
  Comparator #(.width(32), .mode("unsigned")) comparator_2 (
    .a(A), .b(B), .gt(comparator_2_gt[0]), .eq(comparator_2_eq));  // open: lt
  assign nor_1_out = ~(A | B);  // NOR_Gate nor_1, 32 bits wide
  Shifter #(.width(32), .shift("ar")) shifter_1 (.in(A), .\dist (B[4:0]), .out(shifter_1_out));
  Multiplier #(.width(32)) multiplier_1 (.a(A), .b(B), .out(multiplier_1_out));  // open: cin, cout
  Divider #(.width(32)) divider_1 (.a(A), .b(B), .out(divider_1_out), .rem(divider_1_rem));  // open: upper
  Shifter #(.width(32), .shift("lr")) shifter_2 (.in(A), .\dist (B[4:0]), .out(shifter_2_out));
  assign xor_1_out = A ^ B;  // XOR_Gate xor_1, 32 bits wide
  assign and_1_out = A & B;  // AND_Gate and_1, 32 bits wide
  assign xnor_1_out = ~(A ^ B);  // XNOR_Gate xnor_1, 32 bits wide
  Adder #(.width(32)) adder_1 (.a(A), .b(B), .out(adder_1_out));  // open: cin, cout
  assign or_1_out = A | B;  // OR_Gate or_1, 32 bits wide
  Shifter #(.width(32)) shifter_3 (.in(A), .\dist (B[4:0]), .out(shifter_3_out));
  Subtractor #(.width(32)) subtractor_1 (.a(A), .b(B), .out(subtractor_1_out));  // open: bin, bout
  and and_2 (and_2_out[0], Status[1], Status[0]);
  and and_3 (and_3_out[0], comparator_2_gt[0], comparator_2_eq);
  not not_1 (not_1_out[0], comparator_2_eq);
  Multiplexer #(.width(32), .enable("false")) multiplexer_1 (
    .in0(nor_1_out), .in1(shifter_1_out), .out(multiplexer_1_out), .sel(Sel[0]));
  Multiplexer #(.width(32), .enable("false")) multiplexer_2 (
    .in0(multiplier_1_out), .in1(divider_1_out), .out(multiplexer_2_out), .sel(Sel[0]));
  Multiplexer #(.width(32), .enable("false")) multiplexer_3 (
    .in0(xor_1_out), .in1(divider_1_out), .out(multiplexer_3_out), .sel(Sel[0]));
  Multiplexer #(.width(32), .enable("false")) multiplexer_4 (
    .in0(and_1_out), .in1(xnor_1_out), .out(multiplexer_4_out), .sel(Sel[0]));
  Multiplexer #(.width(32), .enable("false")) multiplexer_5 (
    .in0(or_1_out), .in1(shifter_3_out), .out(multiplexer_5_out), .sel(Sel[0]));
  Multiplexer #(.width(32), .enable("false")) multiplexer_6 (
    .in0(and_1_out), .in1({{31{1'b0}}, Status[1]}), .out(multiplexer_6_out), .sel(Sel[0]));
  Multiplexer #(.width(32), .enable("false")) multiplexer_7 (
    .in0({{31{1'b0}}, Status[0]}), .in1({{31{1'b0}}, and_2_out[0]}), .out(multiplexer_7_out), .sel(Sel[0]));
  Multiplexer #(.width(32), .enable("false")) multiplexer_8 (
    .in0({{31{1'b0}}, and_3_out[0]}), .in1({{31{1'b0}}, comparator_2_gt[0]}), .out(multiplexer_8_out),
    .sel(Sel[0]));
  Multiplexer #(.width(32), .enable("false")) multiplexer_9 (
    .in0(or_1_out), .in1({{31{1'b0}}, not_1_out[0]}), .out(multiplexer_9_out), .sel(Sel[0]));
  Multiplexer #(.width(32), .enable("false")) multiplexer_10 (
    .in0(multiplexer_1_out), .in1(multiplexer_2_out), .out(multiplexer_10_out), .sel(Sel[1]));
  Multiplexer #(.width(32), .enable("false")) multiplexer_11 (
    .in0(shifter_2_out), .in1(multiplexer_3_out), .out(multiplexer_11_out), .sel(Sel[1]));
  Multiplexer #(.width(32), .enable("false")) multiplexer_12 (
    .in0(multiplexer_4_out), .in1(adder_1_out), .out(multiplexer_12_out), .sel(Sel[1]));
  Multiplexer #(.width(32), .enable("false")) multiplexer_13 (
    .in0(adder_1_out), .in1(multiplexer_5_out), .out(multiplexer_13_out), .sel(Sel[1]));
  Multiplexer #(.width(32), .enable("false")) multiplexer_14 (
    .in0(divider_1_rem), .in1(subtractor_1_out), .out(multiplexer_14_out), .sel(Sel[1]));
  Multiplexer #(.width(32), .enable("false")) multiplexer_15 (
    .in0(divider_1_rem), .in1(adder_1_out), .out(multiplexer_15_out), .sel(Sel[1]));
  Multiplexer #(.width(32), .enable("false")) multiplexer_16 (
    .in0(multiplexer_6_out), .in1(multiplexer_7_out), .out(multiplexer_16_out), .sel(Sel[1]));
  Multiplexer #(.width(32), .enable("false")) multiplexer_17 (
    .in0(multiplexer_8_out), .in1(multiplexer_9_out), .out(multiplexer_17_out), .sel(Sel[1]));
  Multiplexer #(.width(32), .enable("false")) multiplexer_18 (
    .in0(multiplexer_10_out), .in1(multiplexer_11_out), .out(multiplexer_18_out), .sel(Sel[2]));
  Multiplexer #(.width(32), .enable("false")) multiplexer_19 (
    .in0(multiplexer_12_out), .in1(multiplexer_13_out), .out(multiplexer_19_out), .sel(Sel[2]));
  Multiplexer #(.width(32), .enable("false")) multiplexer_20 (
    .in0(multiplexer_14_out), .in1(multiplexer_15_out), .out(multiplexer_20_out), .sel(Sel[2]));
  Multiplexer #(.width(32), .enable("false")) multiplexer_21 (
    .in0(multiplexer_16_out), .in1(multiplexer_17_out), .out(multiplexer_21_out), .sel(Sel[2]));
  Multiplexer #(.width(32), .enable("false")) multiplexer_22 (
    .in0(multiplexer_18_out), .in1(multiplexer_19_out), .out(multiplexer_22_out), .sel(Sel[3]));
  Multiplexer #(.width(32), .enable("false")) multiplexer_23 (
    .in0(multiplexer_20_out), .in1(multiplexer_21_out), .out(multiplexer_23_out), .sel(Sel[3]));
  Multiplexer #(.width(32), .enable("false")) multiplexer_24 (
    .in0(multiplexer_22_out), .in1(multiplexer_23_out), .out(Result), .sel(Sel[4]));

  assign Status[2] = 1'b0;

  // Notes on the sheet:
  //   Sel: pull=down
  //   MOD
  //   MOD
  //   AND
  //   OR
endmodule

module main (
);

  wire CLK, pull_resistor_5_node, RST;
  wire [1:0] ADMX, fsm_1_out, fsm_1_out_2, fsm_1_out_4, fsm_1_out_5, fsm_1_out_6, fsm_1_out_7, fsm_1_out_8,
       fsm_1_out_9, fsm_1_out_10, RWDMX;
  wire [4:0] multiplexer_4_out;
  wire [9:0] alu_1_status;
  wire [31:0] adder_1_out, ALUR, controlled_buffer_1_out, IR_q, multiplexer_1_out, multiplexer_2_out,
       multiplexer_3_out, multiplexer_5_out, multiplexer_6_out, PC_q, reg32_1_out_9, REGS1;
  wire [31:6] fsm_1_out_3;

  Clock clock_1 (.out(CLK));
  Pull_Resistor pull_resistor_1 (.node(RST));
  Multiplexer #(.select(2), .width(32), .enable("false")) multiplexer_1 (
    .in0(adder_1_out), .in1(REGS1), .in2(ALUR), .out(multiplexer_1_out), .sel(fsm_1_out_3[7:6]));  // open: in3
  Button button_1 (.out(RST));
  Multiplexer #(.select(2), .width(32), .enable("false")) multiplexer_2 (
    .in0(PC_q), .in1(ALUR), .out(multiplexer_2_out), .sel(ADMX));  // open: in2, in3
  Register #(.width(32)) PC (.D(multiplexer_1_out), .en(fsm_1_out_3[31]), .Q(PC_q), .clk(CLK), .clr(RST));
  Register #(.width(32)) IR (.D(controlled_buffer_1_out), .en(fsm_1_out_3[30]), .Q(IR_q), .clk(CLK), .clr(RST));
  Adder #(.width(32)) adder_1 (.a(PC_q), .b(32'h1), .out(adder_1_out));  // open: cin, cout
  Multiplexer #(.select(2), .width(32), .enable("false")) multiplexer_3 (
    .in0(controlled_buffer_1_out), .in1(ALUR), .in2(PC_q), .out(multiplexer_3_out), .sel(RWDMX));  // open: in3
  Pull_Resistor pull_resistor_2 (.node(fsm_1_out_3[26]));
  Multiplexer #(.select(2), .width(5), .enable("false")) multiplexer_4 (
    .in0(IR_q[15:11]), .in1(IR_q[20:16]), .in2(5'b11101), .out(multiplexer_4_out), .sel(fsm_1_out_2));  // open: in3
  REG32 reg32_1 (
    .in_1(multiplexer_4_out), .in_2(IR_q[25:21]), .in_3(IR_q[20:16]), .in_4(fsm_1_out_3[26]), .out_8(REGS1),
    .in_5(multiplexer_3_out), .out_9(reg32_1_out_9), .in_6(CLK), .in_7(RST));
  Pull_Resistor pull_resistor_3 (.node(fsm_1_out_3[28]));
  Pull_Resistor pull_resistor_4 (.node(fsm_1_out_3[29]));
  assign controlled_buffer_1_out = fsm_1_out_3[29] ? reg32_1_out_9 : 32'bz;  // Controlled_Buffer controlled_buffer_1
  FSM fsm_1 (
    .IN({IR_q[31:26], alu_1_status}), .CLK(CLK), .RST(RST),
    .OUT({fsm_1_out_3[31:24], fsm_1_out_10, fsm_1_out_9, fsm_1_out_8, fsm_1_out_7, fsm_1_out_6, fsm_1_out_5, fsm_1_out_4, ADMX, fsm_1_out_3[7:6], RWDMX, fsm_1_out_2, fsm_1_out}));
  RAM #(.addrWidth(16), .dataWidth(32), .bus("separate")) ram_1 (
    .addr(multiplexer_2_out[15:0]), .din(controlled_buffer_1_out), .data(controlled_buffer_1_out),
    .str(fsm_1_out_3[28]), .sel(pull_resistor_5_node), .clk(CLK), .ld(fsm_1_out_3[27]));  // open: clr
  Pull_Resistor #(.pull(1)) pull_resistor_5 (.node(pull_resistor_5_node));
  Pull_Resistor pull_resistor_6 (.node(fsm_1_out_3[27]));
  Multiplexer #(.width(32), .enable("false")) multiplexer_5 (
    .in0(PC_q), .in1(REGS1), .out(multiplexer_5_out), .sel(fsm_1_out_3[25]));
  Multiplexer #(.select(2), .width(32), .enable("false")) multiplexer_6 (
    .in0(reg32_1_out_9), .in1({{16{1'b0}}, IR_q[15:0]}), .in2({IR_q[15:0], {16{1'b0}}}),
    .out(multiplexer_6_out), .sel(fsm_1_out));  // open: in3
  ALU alu_1 (
    .A(multiplexer_5_out), .B(multiplexer_6_out), .Sel(IR_q[30:26]), .Result(ALUR), .Status(alu_1_status[2:0]));
  // Probe on ALUR
  // Probe on alu_1_status[2:0]

  // Notes on the sheet:
  //   Address bus
  //   Data bus
  //   CLK
  //   RST
  //   RA
  //   control FSM output
  //   IMMEDIATE
  //   ROP2 or RIDEST
  //   RRDEST
  //   ROP1
  //   OPCODE
  //   IMM
  //   MAIN SDRAM
  //   control FSM input
endmodule
